# Fritzing sketch ligacao_eletrica (saved by Fritzing 1.0.6)
breadboards: 1

parts:
  LCD1 = LCD screen
  LCM1602_IIC1 = LCM1602 IIC [part_number="LCM1602 IIC" chip_label="LCM1602 IIC" package="DIP (Dual Inline) [THT]"]
  Componente1 = Arduino Nano (Rev3.0)

nets:
  VSS: LCD1.VSS, LCM1602_IIC1.VSS
  VDD: LCD1.VDD, LCM1602_IIC1.VDD
  N1: LCD1.V0, LCM1602_IIC1.V0
  N2: LCD1.RS, LCM1602_IIC1.RS
  N3: LCD1.R/W, LCM1602_IIC1.RW
  N4: LCD1.E, LCM1602_IIC1.E
  N5: LCD1.DB0, LCM1602_IIC1.D0
  N6: LCD1.DB1, LCM1602_IIC1.D1
  N7: LCD1.DB2, LCM1602_IIC1.D2
  N8: LCD1.DB3, LCM1602_IIC1.D3
  N9: LCD1.DB4, LCM1602_IIC1.D4
  N10: LCD1.DB5, LCM1602_IIC1.D5
  N11: LCD1.DB6, LCM1602_IIC1.D6
  N12: LCD1.DB7, LCM1602_IIC1.D7
  N13: LCD1.LED+, LCM1602_IIC1.A
  N14: LCD1.LED-, LCM1602_IIC1.K
  GND: LCM1602_IIC1.GND, Componente1.GND
  VCC: LCM1602_IIC1.VCC, Componente1.5V
  N15: LCM1602_IIC1.SDA, Componente1.A4
  N16: LCM1602_IIC1.SCL, Componente1.A5
  N17: LCM1602_IIC1.LED_A, LCM1602_IIC1.LED_B

custom parts:
  LCM1602 IIC: I2C-Module to use a 1602 or 2004 LCD on with the wire.h libory Serial LCD Modul

// code stored in the sketch: teste-display.ino
#include <Wire.h>
void setup()
{
  Wire.begin();
 
  Serial.begin(9600);
  while (!Serial);             
  Serial.println("\nI2C Scanner");
}
 
void loop()
{
  byte error, address;
  int nDevices;
  nDevices = 0;
  for(address = 1; address < 127; address++ )
  {
    Wire.beginTransmission(address);
    error = Wire.endTransmission();
    if (error == 0)
    {
      Serial.print("Endereço I2C encontrado: 0x");
      if (address<16)
        Serial.print("0 ");
      Serial.println(address,HEX);

 
      nDevices++;
    }
    else if (error==4)
    {
      Serial.print("ERRO ");
      if (address<16)
        Serial.print("0");
      Serial.println(address,HEX);
    }    
  }
  if (nDevices == 0)
    Serial.println("Nenhum endereço i2C encontrado ");
  else
    
    Serial.println(" Feito !");
 
  delay(5000);         
}
